// Logisim project alu.circ as structural Verilog: 1 circuit, main circuit alu
module alu (
  input  [31:0] A,
  input  [31:0] B,
  input  [3:0] ALUSel,
  output [31:0] Result
);

  wire adder_3_cout, comparator_1_lt, comparator_2_eq, xor_2_out, xor_3_out;
  wire [4:0] low_5_of_B;
  wire [5:0] bitadder_1_out, bitadder_2_out;
  wire [31:0] abs_of_A, abs_of_B, adder_4_out, bit_extender_5_out, divider_2_out, multiplier_2_cout,
       multiplier_2_out, negator_1_out, negator_2_out, negator_3_out, not_1_out, not_2_out, number_of_1_A,
       number_of_1_B, out_0_and, out_1_or, out_2_xor, out_3_add, out_4_sub, out_5_mult, out_6_mulhu,
       out_7_mulh, out_8_divu, out_9_div, out_10_remu, out_11_srl, out_12_sra, out_13_slt, out_14_sir,
       out_15_cnto, out_15_sll;

  BitSelector #(.width(32), .group(5)) bitselector_1 (.in(B), .out(low_5_of_B), .sel(3'b000));
  BitAdder #(.width(1)) bitadder_1 (
    .in0(A[0]), .in1(A[1]), .in2(A[2]), .in3(A[3]), .in4(A[4]), .in5(A[5]), .in6(A[6]), .in7(A[7]),
    .in8(A[8]), .in9(A[9]), .in10(A[10]), .in11(A[11]), .in12(A[12]), .in13(A[13]), .in14(A[14]),
    .in15(A[15]), .in16(A[16]), .in17(A[17]), .in18(A[18]), .in19(A[19]), .in20(A[20]), .in21(A[21]),
    .in22(A[22]), .in23(A[23]), .in24(A[24]), .in25(A[25]), .in26(A[26]), .in27(A[27]), .in28(A[28]),
    .in29(A[29]), .in30(A[30]), .in31(A[31]), .out(bitadder_1_out));
  assign number_of_1_A = {{26{1'b0}}, bitadder_1_out};  // Bit_Extender bit_extender_1
  assign out_0_and = A & B;  // AND_Gate and_1, 32 bits wide
  assign out_1_or = A | B;  // OR_Gate or_1, 32 bits wide
  assign out_2_xor = A ^ B;  // XOR_Gate xor_1, 32 bits wide
  Adder #(.width(32)) adder_1 (.a(A), .b(B), .out(out_3_add));  // open: cin, cout
  Subtractor #(.width(32)) subtractor_1 (.a(A), .b(B), .out(out_4_sub));  // open: bin, bout
  Multiplier #(.width(32)) multiplier_1 (.a(A), .b(B), .out(out_5_mult), .cout(out_6_mulhu));  // open: cin
  Shifter #(.width(32)) shifter_1 (.in(A), .\dist (low_5_of_B), .out(out_15_sll));
  BitAdder #(.width(1)) bitadder_2 (
    .in0(B[0]), .in1(B[1]), .in2(B[2]), .in3(B[3]), .in4(B[4]), .in5(B[5]), .in6(B[6]), .in7(B[7]),
    .in8(B[8]), .in9(B[9]), .in10(B[10]), .in11(B[11]), .in12(B[12]), .in13(B[13]), .in14(B[14]),
    .in15(B[15]), .in16(B[16]), .in17(B[17]), .in18(B[18]), .in19(B[19]), .in20(B[20]), .in21(B[21]),
    .in22(B[22]), .in23(B[23]), .in24(B[24]), .in25(B[25]), .in26(B[26]), .in27(B[27]), .in28(B[28]),
    .in29(B[29]), .in30(B[30]), .in31(B[31]), .out(bitadder_2_out));
  assign number_of_1_B = {{26{1'b0}}, bitadder_2_out};  // Bit_Extender bit_extender_2
  Negator #(.width(32)) negator_1 (.in(A), .out(negator_1_out));
  Negator #(.width(32)) negator_2 (.in(B), .out(negator_2_out));
  Divider #(.width(32)) divider_1 (.a(A), .b(B), .out(out_8_divu), .rem(out_10_remu));  // open: upper
  Shifter #(.width(32), .shift("lr")) shifter_2 (.in(A), .\dist (low_5_of_B), .out(out_11_srl));
  Shifter #(.width(32), .shift("ar")) shifter_3 (.in(A), .\dist (low_5_of_B), .out(out_12_sra));
  Comparator #(.width(32)) comparator_1 (.a(A), .b(B), .lt(comparator_1_lt));  // open: gt, eq
  Comparator #(.width(32), .mode("unsigned")) comparator_2 (
    .a({A[0], A[1], A[2], A[3], A[4], A[5], A[6], A[7], A[8], A[9], A[10], A[11], A[12], A[13], A[14], A[15], A[16], A[17], A[18], A[19], A[20], A[21], A[22], A[23], A[24], A[25], A[26], A[27], A[28], A[29], A[30], A[31]}),
    .b(B), .eq(comparator_2_eq));  // open: gt, lt
  Adder #(.width(32)) adder_2 (.a(number_of_1_A), .b(number_of_1_B), .out(out_15_cnto));  // open: cin, cout
  Multiplexer #(.width(32), .enable("false")) multiplexer_1 (.in0(A), .in1(negator_1_out), .out(abs_of_A), .sel(A[31]));
  Multiplexer #(.width(32), .enable("false")) multiplexer_2 (.in0(B), .in1(negator_2_out), .out(abs_of_B), .sel(B[31]));
  assign out_13_slt = {{31{1'b0}}, comparator_1_lt};  // Bit_Extender bit_extender_3
  assign out_14_sir = {{31{1'b0}}, comparator_2_eq};  // Bit_Extender bit_extender_4
  Multiplier #(.width(32)) multiplier_2 (
    .a(abs_of_A), .b(abs_of_B), .out(multiplier_2_out), .cout(multiplier_2_cout));  // open: cin
  Divider #(.width(32)) divider_2 (.a(abs_of_A), .b(abs_of_B), .out(divider_2_out));  // open: upper, rem
  assign not_1_out = ~multiplier_2_out;  // NOT_Gate not_1, 32 bits wide
  assign not_2_out = ~multiplier_2_cout;  // NOT_Gate not_2, 32 bits wide
  Negator #(.width(32)) negator_3 (.in(divider_2_out), .out(negator_3_out));
  xor xor_2 (xor_2_out, A[31], B[31]);
  Adder #(.width(32)) adder_3 (.a(not_1_out), .b(32'h1), .cout(adder_3_cout));  // open: out, cin
  assign bit_extender_5_out = {{31{1'b0}}, adder_3_cout};  // Bit_Extender bit_extender_5
  Multiplexer #(.width(32), .enable("false")) multiplexer_3 (
    .in0(divider_2_out), .in1(negator_3_out), .out(out_9_div), .sel(xor_2_out));
  Multiplexer #(.select(4), .width(32), .enable("false")) multiplexer_4 (
    .in0(out_0_and), .in1(out_1_or), .in2(out_2_xor), .in3(out_3_add), .in4(out_4_sub), .in5(out_5_mult),
    .in6(out_6_mulhu), .in7(out_7_mulh), .in8(out_8_divu), .in9(out_9_div), .in10(out_10_remu),
    .in11(out_11_srl), .in12(out_12_sra), .in13(out_13_slt), .in14(out_14_sir), .in15(out_15_sll),
    .out(Result), .sel(ALUSel));
  Adder #(.width(32)) adder_4 (.a(bit_extender_5_out), .b(not_2_out), .out(adder_4_out));  // open: cin, cout
  xor xor_3 (xor_3_out, A[31], B[31]);
  Multiplexer #(.width(32), .enable("false")) multiplexer_5 (
    .in0(multiplier_2_cout), .in1(adder_4_out), .out(out_7_mulh), .sel(xor_3_out));

  // Other names for the same wires on the sheet: sign_of_B = B[31];
  //   reversed_A[31:0] = {A[0], A[1], A[2], A[3], A[4], A[5], A[6], A[7], A[8], A[9], A[10], A[11], A[12], A[13], A[14], A[15], A[16], A[17], A[18], A[19], A[20], A[21], A[22], A[23], A[24], A[25], A[26], A[27], A[28], A[29], A[30], A[31]};
  //   sign_of_A = A[31]

  // Notes on the sheet:
  //   INPUTS to your circuit
  //   DON'T CHANGE THE LOCATIONS OF THE INPUTS AND OUTPUTS!
  //   OUTPUT from your circuit
endmodule
