// Logisim project cpu.circ as structural Verilog: 5 circuits, main circuit main
module main (
  input  [31:0] INSTRUCTION,
  input  CLOCK,
  output [31:0] FETCH_ADDRESS,
  output [31:0] ra,
  output [31:0] sp,
  output [31:0] t0,
  output [31:0] t1,
  output [31:0] t2,
  output [31:0] s0,
  output [31:0] s1,
  output [31:0] a0
);

  wire BrEq, BrLT, BrUn, BSel, MemRW, PCSel, RegWEn;
  wire [1:0] ASel, WBSel;
  wire [2:0] DataSel, ImmSel;
  wire [3:0] ALUSel;
  wire [31:0] adder_1_out, adder_2_out, ALUResult, bit_extender_1_out, bit_extender_2_out,
       bit_extender_3_out, bit_extender_4_out, DMEM_readdata, imm, INST, MEMData, multiplexer_1_out,
       multiplexer_2_out, multiplexer_3_out, multiplexer_4_out, PC_f, PC_p3, PC_plus_4, PC_x, rs1, rs2,
       WriteData;

  Adder #(.width(32)) adder_1 (.a(PC_p3), .b(32'h1), .out(adder_1_out));  // open: cin, cout
  Adder #(.width(32)) adder_2 (.a(PC_f), .b(32'h4), .out(adder_2_out));  // open: cin, cout
  // Register #(.width(32)) PC: pin names not known; wires that end beside it: adder_1_out, CLOCK, PC_p3
  Register #(.width(32)) register_1 (.D(multiplexer_1_out), .clk(CLOCK), .Q(PC_f));  // open: en, clr
  Multiplexer #(.width(32), .enable("false")) multiplexer_1 (
    .in0(adder_2_out), .in1(ALUResult), .out(multiplexer_1_out), .sel(PCSel));
  Register #(.width(32)) PC_d (.D(PC_f), .clk(CLOCK), .Q(PC_x));  // open: en, clr
  Multiplexer #(.width(32), .enable("false")) multiplexer_2 (
    .in0(INSTRUCTION), .in1(32'h13), .out(multiplexer_2_out), .sel(PCSel));
  Register #(.width(32)) Inst_d (.D(multiplexer_2_out), .clk(CLOCK), .Q(INST));  // open: en, clr
  Shifter #(.width(32), .shift("lr")) shifter_1 (.in(PC_f), .\dist (5'b00010), .out(FETCH_ADDRESS));
  Controller controller_1 (
    .Instruction_input(INST), .BrEq_input(BrEq), .BrLT_input(BrLT), .ALUsel_output(ALUSel),
    .Asel_output(ASel), .Bsel_output(BSel), .MemRW_output(MemRW), .PCSel_output(PCSel),
    .ImmSel_output(ImmSel), .BrUn_output(BrUn), .RegWEn_output(RegWEn), .WBSel_output(WBSel),
    .DataSel_output(DataSel));
  Multiplexer #(.select(2), .width(32), .enable("false")) multiplexer_3 (
    .in0(rs1), .in1(PC_x), .in2({32{1'b0}}), .out(multiplexer_3_out), .sel(ASel));  // open: in3
  Multiplexer #(.width(32), .enable("false")) multiplexer_4 (.in0(rs2), .in1(imm), .out(multiplexer_4_out), .sel(BSel));
  Adder #(.width(32)) adder_3 (.a(PC_x), .b(32'h4), .out(PC_plus_4));  // open: cin, cout
  mem_main DMEM (.WriteAddr(ALUResult), .WriteData(rs2), .MemRW(MemRW), .ReadData(DMEM_readdata), .clk(CLOCK));
  Immediate_gen immediate_gen_1 (.Imm_sel(ImmSel), .Instruction_input(INST), .Imm_output(imm));
  alu Arithmetic_Logic_Unit (.A(multiplexer_3_out), .B(multiplexer_4_out), .ALUSel(ALUSel), .Result(ALUResult));
  Branch_comparator branch_comparator_1 (
    .Input_dataA(rs1), .Input_dataB(rs2), .Input_BrUn(BrUn), .Output_BrEq(BrEq), .Output_BrLT(BrLT));
  assign bit_extender_1_out = {{24{DMEM_readdata[7]}}, DMEM_readdata[7:0]};  // Bit_Extender bit_extender_1
  assign bit_extender_2_out = {{16{DMEM_readdata[15]}}, DMEM_readdata[15:0]};  // Bit_Extender bit_extender_2
  assign bit_extender_3_out = {{24{1'b0}}, DMEM_readdata[7:0]};  // Bit_Extender bit_extender_3
  assign bit_extender_4_out = {{16{1'b0}}, DMEM_readdata[15:0]};  // Bit_Extender bit_extender_4
  regfile_main RegFile (
    .rs2(INST[24:20]), .rd(INST[11:7]), .Read_Data_1(rs1), .Read_Data_2(rs2), .ra(ra), .sp(sp), .t0(t0),
    .t1(t1), .t2(t2), .s0(s0), .s1(s1), .a0(a0), .rs1(INST[19:15]), .Write_Data(WriteData), .RegWEn(RegWEn),
    .clk(CLOCK));
  Multiplexer #(.select(3), .width(32), .enable("false")) multiplexer_5 (
    .in0(bit_extender_1_out), .in1(bit_extender_2_out), .in2(DMEM_readdata), .in3(bit_extender_3_out),
    .in4(bit_extender_4_out), .out(MEMData), .sel(DataSel));  // open: in5, in6, in7
  Multiplexer #(.select(2), .width(32), .enable("false")) multiplexer_6 (
    .in0(MEMData), .in1(ALUResult), .in2(PC_plus_4), .out(WriteData), .sel(WBSel));  // open: in3

  // Other names for the same wires on the sheet: a0_x10[31:0] = a0; clk = CLOCK; fetch_addr[31:0] = FETCH_ADDRESS;
  //   reg_rd[4:0] = INST[11:7]; reg_rs1[4:0] = INST[19:15]; reg_rs2[4:0] = INST[24:20]; ra_x1[31:0] = ra;
  //   s0_x8[31:0] = s0; s1_x9[31:0] = s1; sp_x2[31:0] = sp; t0_x5[31:0] = t0; t1_x6[31:0] = t1; t2_x7[31:0] = t2

  // Notes on the sheet:
  //   Output
  //   Inputs/Outputs from run.circ. DO NOT MOVE THESE.
  //   Similarly, the register below is holding the instruction temporarily
  //   then we immediately kill it (before execute) by inserting 0x00000013 NOP
  //   Inputs
  //   [Deprecated] Provided Instruction fetch Unit
  //   IF: Instruction fetch and register after IF
  //   We will always use address in bytes, except that, when we output to fetch_addr, use address in word
  //   The register above is between IF stage and the rest 4 stages, responsible for holding PC state
  //   If the previous instruction takes a branch (PCSel=1),
  //   Controller
  //   Instruction Decode, Register Read and Immediate Generate
  //   Execute: ALU select and operation
  //   Execute: Branch Compare operation
  //   Memory (RAM) read or write 
  //   Remember that, in controller, DataSel = 0,1,2,3,4 means Byte, Half, Original, ByteUnsigned, HalfUnsigned
  //   Write Back(to register)
  //   Write back to register. Selections are: memory, ALU and PC+4, corresponding to 0,1,2
  //   Inputs/Outputs from run.circ. DO NOT MOVE THESE.
endmodule

module Controller (
  input  [31:0] Instruction_input,
  input  BrEq_input,
  input  BrLT_input,
  output [3:0] ALUsel_output,
  output [1:0] Asel_output,
  output Bsel_output,
  output MemRW_output,
  output PCSel_output,
  output [2:0] ImmSel_output,
  output BrUn_output,
  output RegWEn_output,
  output [1:0] WBSel_output,
  output [2:0] DataSel_output
);

  wire and_12_out, and_13_out, and_14_out, and_15_out, and_16_out, and_25_out, Btype, comparator_10_gt,
       comparator_11_eq, comparator_12_eq, comparator_13_eq, comparator_14_eq, comparator_15_eq,
       comparator_16_eq, comparator_17_eq, comparator_18_eq, comparator_19_eq, comparator_20_eq,
       comparator_21_eq, comparator_22_eq, comparator_23_eq, comparator_24_eq, comparator_25_eq,
       comparator_26_eq, comparator_27_eq, ItypeAri, ItypeJalr, ItypeLd, Jtype, not_1_out, not_4_out,
       not_5_out, not_6_out, or_1_out, or_2_out, or_3_out, or_4_out, or_5_out, or_6_out, or_10_out,
       or_11_out, Rtype, UtypeAuipc, UtypeLui;
  wire [1:0] and_6_out, and_7_out, and_9_out, and_10_out, and_11_out, bit_extender_6_out, bit_extender_7_out,
       bit_extender_8_out, bit_extender_9_out, bit_extender_10_out;
  wire [2:0] and_1_out, and_2_out, and_3_out, and_4_out, and_5_out, and_20_out, and_21_out, and_22_out,
       and_23_out, and_24_out, bit_extender_1_out, bit_extender_2_out, bit_extender_3_out,
       bit_extender_4_out, bit_extender_5_out, bit_extender_14_out, bit_extender_15_out, bit_extender_16_out,
       bit_extender_17_out, bit_extender_18_out, or_14_out;
  wire [3:0] and_17_out, and_18_out, and_19_out, bit_extender_11_out, bit_extender_12_out,
       bit_extender_13_out, ItypeAri_ALUsel, multiplexer_1_out, multiplexer_2_out, multiplexer_3_out,
       multiplexer_4_out, multiplexer_5_out, multiplexer_6_out, multiplexer_7_out, Rtype_ALUsel;

  Comparator #(.width(7)) comparator_1 (.a(Instruction_input[6:0]), .b(7'b0110011), .eq(Rtype));  // open: gt, lt
  Comparator #(.width(7)) comparator_2 (.a(Instruction_input[6:0]), .b(7'b0010011), .eq(ItypeAri));  // open: gt, lt
  Comparator #(.width(7)) comparator_3 (.a(Instruction_input[6:0]), .b(7'b0000011), .eq(ItypeLd));  // open: gt, lt
  Comparator #(.width(7)) comparator_4 (.a(Instruction_input[6:0]), .b(7'b1100111), .eq(ItypeJalr));  // open: gt, lt
  Comparator #(.width(7)) comparator_5 (.a(Instruction_input[6:0]), .b(7'b0100011), .eq(MemRW_output));  // open: gt, lt
  Comparator #(.width(7)) comparator_6 (.a(Instruction_input[6:0]), .b(7'b0110111), .eq(UtypeLui));  // open: gt, lt
  Comparator #(.width(7)) comparator_7 (.a(Instruction_input[6:0]), .b(7'b0010111), .eq(UtypeAuipc));  // open: gt, lt
  Comparator #(.width(7)) comparator_8 (.a(Instruction_input[6:0]), .b(7'b1100011), .eq(Btype));  // open: gt, lt
  Comparator #(.width(7)) comparator_9 (.a(Instruction_input[6:0]), .b(7'b1101111), .eq(Jtype));  // open: gt, lt
  assign bit_extender_1_out = {{2{or_1_out}}, or_1_out};  // Bit_Extender bit_extender_1
  or or_1 (or_1_out, ItypeAri, ItypeLd, ItypeJalr);
  assign bit_extender_2_out = {{2{MemRW_output}}, MemRW_output};  // Bit_Extender bit_extender_2
  assign bit_extender_3_out = {{2{Btype}}, Btype};  // Bit_Extender bit_extender_3
  assign bit_extender_4_out = {{2{or_2_out}}, or_2_out};  // Bit_Extender bit_extender_4
  or or_2 (or_2_out, UtypeLui, UtypeAuipc);
  assign bit_extender_5_out = {{2{Jtype}}, Jtype};  // Bit_Extender bit_extender_5
  or or_3 (or_3_out, Btype, Jtype, UtypeAuipc);
  or or_4 (or_4_out, ItypeJalr, Jtype);
  not not_1 (not_1_out, or_5_out);
  or or_5 (or_5_out, ItypeLd, ItypeJalr, Jtype);
  assign and_1_out = bit_extender_1_out & 3'b000;  // AND_Gate and_1, 3 bits wide
  assign and_2_out = bit_extender_2_out & 3'b001;  // AND_Gate and_2, 3 bits wide
  assign and_3_out = bit_extender_3_out & 3'b010;  // AND_Gate and_3, 3 bits wide
  assign and_4_out = bit_extender_4_out & 3'b011;  // AND_Gate and_4, 3 bits wide
  assign and_5_out = bit_extender_5_out & 3'b100;  // AND_Gate and_5, 3 bits wide
  or or_6 (or_6_out, MemRW_output, Btype);
  assign bit_extender_6_out = {{1{or_3_out}}, or_3_out};  // Bit_Extender bit_extender_6
  assign bit_extender_7_out = {{1{UtypeLui}}, UtypeLui};  // Bit_Extender bit_extender_7
  not not_2 (Bsel_output, Rtype);
  Comparator #(.width(3), .mode("unsigned")) comparator_10 (
    .a(Instruction_input[14:12]), .b(3'b101), .gt(comparator_10_gt));  // open: eq, lt
  assign bit_extender_8_out = {{1{ItypeLd}}, ItypeLd};  // Bit_Extender bit_extender_8
  assign bit_extender_9_out = {{1{or_4_out}}, or_4_out};  // Bit_Extender bit_extender_9
  assign bit_extender_10_out = {{1{not_1_out}}, not_1_out};  // Bit_Extender bit_extender_10
  not not_3 (RegWEn_output, or_6_out);
  assign and_6_out = bit_extender_6_out & 2'b01;  // AND_Gate and_6, 2 bits wide
  assign and_7_out = bit_extender_7_out & 2'b10;  // AND_Gate and_7, 2 bits wide
  and and_8 (BrUn_output, Btype, comparator_10_gt);
  assign and_9_out = bit_extender_8_out & 2'b00;  // AND_Gate and_9, 2 bits wide
  assign and_10_out = bit_extender_9_out & 2'b10;  // AND_Gate and_10, 2 bits wide
  assign and_11_out = bit_extender_10_out & 2'b01;  // AND_Gate and_11, 2 bits wide
  assign ImmSel_output = and_1_out | and_2_out | and_3_out | and_4_out | and_5_out;  // OR_Gate or_7, 3 bits wide
  assign Asel_output = and_6_out | and_7_out;  // OR_Gate or_8, 2 bits wide
  assign WBSel_output = and_9_out | and_10_out | and_11_out;  // OR_Gate or_9, 2 bits wide
  or or_10 (or_10_out, Rtype, ItypeAri);
  not not_4 (not_4_out, or_10_out);
  Comparator #(.width(3)) comparator_11 (
    .a(Instruction_input[14:12]), .b(3'b000), .eq(comparator_11_eq));  // open: gt, lt
  Comparator #(.width(3)) comparator_12 (
    .a(Instruction_input[14:12]), .b(3'b001), .eq(comparator_12_eq));  // open: gt, lt
  Comparator #(.width(3)) comparator_13 (
    .a(Instruction_input[14:12]), .b(3'b010), .eq(comparator_13_eq));  // open: gt, lt
  Comparator #(.width(3)) comparator_14 (
    .a(Instruction_input[14:12]), .b(3'b100), .eq(comparator_14_eq));  // open: gt, lt
  Comparator #(.width(3)) comparator_15 (
    .a(Instruction_input[14:12]), .b(3'b101), .eq(comparator_15_eq));  // open: gt, lt
  Comparator #(.width(3)) comparator_16 (
    .a(Instruction_input[14:12]), .b(3'b110), .eq(comparator_16_eq));  // open: gt, lt
  Comparator #(.width(3)) comparator_17 (
    .a(Instruction_input[14:12]), .b(3'b111), .eq(comparator_17_eq));  // open: gt, lt
  Comparator #(.width(3)) comparator_18 (
    .a(Instruction_input[14:12]), .b(3'b000), .eq(comparator_18_eq));  // open: gt, lt
  Comparator #(.width(3)) comparator_19 (
    .a(Instruction_input[14:12]), .b(3'b100), .eq(comparator_19_eq));  // open: gt, lt
  Comparator #(.width(3)) comparator_20 (
    .a(Instruction_input[14:12]), .b(3'b110), .eq(comparator_20_eq));  // open: gt, lt
  not not_5 (not_5_out, BrEq_input);
  Comparator #(.width(3)) comparator_21 (
    .a(Instruction_input[14:12]), .b(3'b001), .eq(comparator_21_eq));  // open: gt, lt
  not not_6 (not_6_out, BrLT_input);
  Comparator #(.width(3)) comparator_22 (
    .a(Instruction_input[14:12]), .b(3'b111), .eq(comparator_22_eq));  // open: gt, lt
  Comparator #(.width(3), .mode("unsigned")) comparator_23 (
    .a(Instruction_input[14:12]), .b(3'b000), .eq(comparator_23_eq));  // open: gt, lt
  Comparator #(.width(3), .mode("unsigned")) comparator_24 (
    .a(Instruction_input[14:12]), .b(3'b001), .eq(comparator_24_eq));  // open: gt, lt
  Comparator #(.width(3), .mode("unsigned")) comparator_25 (
    .a(Instruction_input[14:12]), .b(3'b010), .eq(comparator_25_eq));  // open: gt, lt
  Comparator #(.width(3), .mode("unsigned")) comparator_26 (
    .a(Instruction_input[14:12]), .b(3'b100), .eq(comparator_26_eq));  // open: gt, lt
  Comparator #(.width(3), .mode("unsigned")) comparator_27 (
    .a(Instruction_input[14:12]), .b(3'b101), .eq(comparator_27_eq));  // open: gt, lt
  assign bit_extender_11_out = {{3{Rtype}}, Rtype};  // Bit_Extender bit_extender_11
  assign bit_extender_12_out = {{3{ItypeAri}}, ItypeAri};  // Bit_Extender bit_extender_12
  assign bit_extender_13_out = {{3{not_4_out}}, not_4_out};  // Bit_Extender bit_extender_13
  Multiplexer #(.width(4), .enable("false")) multiplexer_1 (
    .in0(4'b0000), .in1(4'b0011), .out(multiplexer_1_out), .sel(comparator_11_eq));
  Multiplexer #(.width(4), .enable("false")) multiplexer_2 (
    .in0(4'b0000), .in1(4'b1111), .out(multiplexer_2_out), .sel(comparator_12_eq));
  Multiplexer #(.width(4), .enable("false")) multiplexer_3 (
    .in0(4'b0000), .in1(4'b1101), .out(multiplexer_3_out), .sel(comparator_13_eq));
  Multiplexer #(.width(4), .enable("false")) multiplexer_4 (
    .in0(4'b0000), .in1(4'b0010), .out(multiplexer_4_out), .sel(comparator_14_eq));
  Multiplexer #(.width(4), .enable("false")) multiplexer_5 (
    .in0(4'b0000), .in1(4'b1011), .out(multiplexer_5_out), .sel(comparator_15_eq));
  Multiplexer #(.width(4), .enable("false")) multiplexer_6 (
    .in0(4'b0000), .in1(4'b0001), .out(multiplexer_6_out), .sel(comparator_16_eq));
  Multiplexer #(.width(4), .enable("false")) multiplexer_7 (
    .in0(4'b0000), .in1(4'b0000), .out(multiplexer_7_out), .sel(comparator_17_eq));
  and and_12 (and_12_out, BrEq_input, comparator_18_eq);
  and and_13 (and_13_out, BrLT_input, comparator_19_eq);
  and and_14 (and_14_out, BrLT_input, comparator_20_eq);
  and and_15 (and_15_out, not_5_out, comparator_21_eq);
  and and_16 (and_16_out, not_6_out, comparator_22_eq);
  assign bit_extender_14_out = {{2{comparator_23_eq}}, comparator_23_eq};  // Bit_Extender bit_extender_14
  assign bit_extender_15_out = {{2{comparator_24_eq}}, comparator_24_eq};  // Bit_Extender bit_extender_15
  assign bit_extender_16_out = {{2{comparator_25_eq}}, comparator_25_eq};  // Bit_Extender bit_extender_16
  assign bit_extender_17_out = {{2{comparator_26_eq}}, comparator_26_eq};  // Bit_Extender bit_extender_17
  assign bit_extender_18_out = {{2{comparator_27_eq}}, comparator_27_eq};  // Bit_Extender bit_extender_18
  assign and_17_out = bit_extender_11_out & Rtype_ALUsel;  // AND_Gate and_17, 4 bits wide
  assign and_18_out = bit_extender_12_out & ItypeAri_ALUsel;  // AND_Gate and_18, 4 bits wide
  assign and_19_out = bit_extender_13_out & 4'b0011;  // AND_Gate and_19, 4 bits wide
  or or_11 (or_11_out, and_12_out, and_13_out, and_14_out, and_15_out, and_16_out);
  assign and_20_out = bit_extender_14_out & 3'b000;  // AND_Gate and_20, 3 bits wide
  assign and_21_out = bit_extender_15_out & 3'b001;  // AND_Gate and_21, 3 bits wide
  assign and_22_out = bit_extender_16_out & 3'b010;  // AND_Gate and_22, 3 bits wide
  assign and_23_out = bit_extender_17_out & 3'b011;  // AND_Gate and_23, 3 bits wide
  assign and_24_out = bit_extender_18_out & 3'b100;  // AND_Gate and_24, 3 bits wide
  assign ALUsel_output = and_17_out | and_18_out | and_19_out;  // OR_Gate or_12, 4 bits wide
  Controller_RtypeALUSel controller_rtypealusel_1 (
    .funct3_input(Instruction_input[14:12]), .funct7_input(Instruction_input[31:25]),
    .ALUSel_output(Rtype_ALUsel));
  assign ItypeAri_ALUsel = multiplexer_1_out | multiplexer_2_out | multiplexer_3_out | multiplexer_4_out | multiplexer_5_out | multiplexer_6_out | multiplexer_7_out;  // OR_Gate or_13, 4 bits wide
  and and_25 (and_25_out, Btype, or_11_out);
  assign or_14_out = and_20_out | and_21_out | and_22_out | and_23_out | and_24_out;  // OR_Gate or_14, 3 bits wide
  or or_15 (PCSel_output, Jtype, and_25_out, ItypeJalr);
  Multiplexer #(.width(3), .enable("false")) multiplexer_8 (
    .in0(3'b010), .in1(or_14_out), .out(DataSel_output), .sel(ItypeLd));

  // Other names for the same wires on the sheet: ALUsel[3:0] = ALUsel_output; Asel[1:0] = Asel_output;
  //   BrEq = BrEq_input; BrLT = BrLT_input; BrUn = BrUn_output; Bsel = Bsel_output; DataSel[2:0] = DataSel_output;
  //   ImmSel[2:0] = ImmSel_output; INSTRUCTION[31:0] = Instruction_input; opcode[6:0] = Instruction_input[6:0];
  //   funct3[2:0] = Instruction_input[14:12]; funct7[6:0] = Instruction_input[31:25]; PCSel = PCSel_output;
  //   RegWEn = RegWEn_output; MemRW = MemRW_output; Stype = MemRW_output; WBSel[1:0] = WBSel_output

  // Notes on the sheet:
  //   Input To Controller
  //   Output From Controller
  //   Get Opcode, fun3, fun7
  //   Judge the instruction type
  //   Otherwise, Asel = 0 means from Register[rs1]
  //   Immediate Select
  //   000, 001, 010, 011, 100 corresponding to I S B U J
  //   Register Write Enable Select
  //   Other than B-type and S-type, 'register-write' should always be enabled
  //   A select
  //   Asel = 1 means from PC, Asel = 2 means from zero (for LUI use),
  //   Other than LUI and B-type, J-type, AUIPC, Asel should always be zero.
  //   B select
  //   0, 1 corresponding to Register[rs2], Immdiate gen
  //   Only R-type instructions want the ALU to take in Register[rs2]
  //   Branch-unsigned Select
  //   When it's B-type and funct3 is 6 or 7 (larger than 5 in implementation), Branch Unsigned
  //   Memory Read_or_Write Select
  //   Only S-type will need to write to memory!
  //   Write Back Select
  //   0-mem, 1-ALU, 2-PC+4
  //   Load I type should be 0, J-type and JALR should be 2, and all the other are 1
  //   R-type ALUsel
  //   PC select
  //   PCSel = 1 means ALU, PCSel = 0 means PC+4
  //   ALU select
  //   Other than R-type or I-type-arithmetic, ALUsel should always be 3 (add)
  //   Arithmetic I-type ALUsel
  //   If B-type and branch taken, or JALR or J-type, PCsel should set to 1.
  //   Data Select (original word, or half or byte)
  //   DataSel = 0,1,2,3,4 means Byte, Half, Original, ByteUnsigned, HalfUnsigned
  //   In I-type-load, funct3 = 0,1,2,4,5 means lb, lh, lw, lbu, lhu
  //   Other than I-type load, the output should always be 2
endmodule

module Immediate_gen (
  input  [2:0] Imm_sel,
  input  [31:0] Instruction_input,
  output [31:0] Imm_output
);

  wire [31:0] bit_extender_1_out, bit_extender_2_out, bit_extender_3_out, bit_extender_4_out;

  assign bit_extender_1_out = {{20{Instruction_input[31]}}, Instruction_input[31:20]};  // Bit_Extender bit_extender_1
  assign bit_extender_2_out = {{20{Instruction_input[31]}}, {Instruction_input[31:25], Instruction_input[11:7]}};  // Bit_Extender bit_extender_2
  assign bit_extender_3_out = {{19{Instruction_input[31]}}, {Instruction_input[31], Instruction_input[7], Instruction_input[30:25], Instruction_input[11:8], 1'b0}};  // Bit_Extender bit_extender_3
  assign bit_extender_4_out = {{11{Instruction_input[31]}}, {Instruction_input[31], Instruction_input[19:12], Instruction_input[20], Instruction_input[30:21], 1'b0}};  // Bit_Extender bit_extender_4
  Multiplexer #(.select(3), .width(32), .enable("false")) multiplexer_1 (
    .in0(bit_extender_1_out), .in1(bit_extender_2_out), .in2(bit_extender_3_out),
    .in3({Instruction_input[31:12], {12{1'b0}}}), .in4(bit_extender_4_out), .out(Imm_output), .sel(Imm_sel));  // open: in5, in6, in7

  // Other names for the same wires on the sheet: Inst_31_7[24:0] = Instruction_input[31:7];
  //   Instruction[31:0] = Instruction_input

  // Notes on the sheet:
  //   I
  //   S
  //   B
  //   U
  //   J
  //   Input to and Output from the Immediate Generator
endmodule

module Controller_RtypeALUSel (
  input  [2:0] funct3_input,
  input  [6:0] funct7_input,
  output [3:0] ALUSel_output
);

  wire AluSel_0, AluSel_1, AluSel_2, AluSel_3, AluSel_4, AluSel_5, AluSel_6, AluSel_7, AluSel_8, AluSel_9,
       AluSel_10, AluSel_11, AluSel_15, comparator_1_eq, comparator_2_eq, comparator_3_eq, comparator_4_eq,
       comparator_5_eq, comparator_6_eq, comparator_7_eq, comparator_8_eq, comparator_9_eq, comparator_10_eq,
       comparator_11_eq, comparator_12_eq, comparator_13_eq, comparator_14_eq, comparator_15_eq,
       comparator_16_eq, comparator_17_eq, comparator_18_eq, comparator_19_eq, comparator_20_eq;
  wire [3:0] multiplexer_1_out, multiplexer_2_out, multiplexer_3_out, multiplexer_4_out, multiplexer_5_out,
       multiplexer_6_out, multiplexer_7_out, multiplexer_8_out, multiplexer_9_out, multiplexer_10_out,
       multiplexer_11_out, multiplexer_12_out, multiplexer_13_out;

  Comparator #(.width(3)) comparator_1 (.a(funct3_input), .b(3'b000), .eq(comparator_1_eq));  // open: gt, lt
  Comparator #(.width(3)) comparator_2 (.a(funct3_input), .b(3'b001), .eq(comparator_2_eq));  // open: gt, lt
  Comparator #(.width(3)) comparator_3 (.a(funct3_input), .b(3'b011), .eq(comparator_3_eq));  // open: gt, lt
  Comparator #(.width(3)) comparator_4 (.a(funct3_input), .b(3'b100), .eq(comparator_4_eq));  // open: gt, lt
  Comparator #(.width(3)) comparator_5 (.a(funct3_input), .b(3'b101), .eq(comparator_5_eq));  // open: gt, lt
  Comparator #(.width(3)) comparator_6 (.a(funct3_input), .b(3'b110), .eq(comparator_6_eq));  // open: gt, lt
  Comparator #(.width(3)) comparator_7 (.a(funct3_input), .b(3'b111), .eq(comparator_7_eq));  // open: gt, lt
  Comparator #(.width(7)) comparator_8 (.a(funct7_input), .b({7{1'b0}}), .eq(comparator_8_eq));  // open: gt, lt
  Comparator #(.width(7)) comparator_9 (.a(funct7_input), .b(7'b0000001), .eq(comparator_9_eq));  // open: gt, lt
  Comparator #(.width(7)) comparator_10 (.a(funct7_input), .b(7'b0100000), .eq(comparator_10_eq));  // open: gt, lt
  Comparator #(.width(7)) comparator_11 (.a(funct7_input), .b({7{1'b0}}), .eq(comparator_11_eq));  // open: gt, lt
  Comparator #(.width(7)) comparator_12 (.a(funct7_input), .b(7'b0000001), .eq(comparator_12_eq));  // open: gt, lt
  Comparator #(.width(7)) comparator_13 (.a(funct7_input), .b(7'b0000001), .eq(comparator_13_eq));  // open: gt, lt
  Comparator #(.width(7)) comparator_14 (.a(funct7_input), .b({7{1'b0}}), .eq(comparator_14_eq));  // open: gt, lt
  Comparator #(.width(7)) comparator_15 (.a(funct7_input), .b(7'b0000001), .eq(comparator_15_eq));  // open: gt, lt
  Comparator #(.width(7)) comparator_16 (.a(funct7_input), .b(7'b0000001), .eq(comparator_16_eq));  // open: gt, lt
  Comparator #(.width(7)) comparator_17 (.a(funct7_input), .b({7{1'b0}}), .eq(comparator_17_eq));  // open: gt, lt
  Comparator #(.width(7)) comparator_18 (.a(funct7_input), .b({7{1'b0}}), .eq(comparator_18_eq));  // open: gt, lt
  Comparator #(.width(7)) comparator_19 (.a(funct7_input), .b(7'b0000001), .eq(comparator_19_eq));  // open: gt, lt
  Comparator #(.width(7)) comparator_20 (.a(funct7_input), .b({7{1'b0}}), .eq(comparator_20_eq));  // open: gt, lt
  and and_1 (AluSel_3, comparator_1_eq, comparator_8_eq);
  and and_2 (AluSel_5, comparator_1_eq, comparator_9_eq);
  and and_3 (AluSel_4, comparator_1_eq, comparator_10_eq);
  and and_4 (AluSel_15, comparator_2_eq, comparator_11_eq);
  and and_5 (AluSel_7, comparator_2_eq, comparator_12_eq);
  and and_6 (AluSel_6, comparator_3_eq, comparator_13_eq);
  and and_7 (AluSel_2, comparator_4_eq, comparator_14_eq);
  and and_8 (AluSel_9, comparator_4_eq, comparator_15_eq);
  and and_9 (AluSel_8, comparator_5_eq, comparator_16_eq);
  and and_10 (AluSel_11, comparator_5_eq, comparator_17_eq);
  and and_11 (AluSel_1, comparator_6_eq, comparator_18_eq);
  and and_12 (AluSel_10, comparator_7_eq, comparator_19_eq);
  and and_13 (AluSel_0, comparator_7_eq, comparator_20_eq);
  Multiplexer #(.width(4), .enable("false")) multiplexer_1 (
    .in0(4'b0000), .in1(4'b0011), .out(multiplexer_1_out), .sel(AluSel_3));
  Multiplexer #(.width(4), .enable("false")) multiplexer_2 (
    .in0(4'b0000), .in1(4'b0101), .out(multiplexer_2_out), .sel(AluSel_5));
  Multiplexer #(.width(4), .enable("false")) multiplexer_3 (
    .in0(4'b0000), .in1(4'b0100), .out(multiplexer_3_out), .sel(AluSel_4));
  Multiplexer #(.width(4), .enable("false")) multiplexer_4 (
    .in0(4'b0000), .in1(4'b1111), .out(multiplexer_4_out), .sel(AluSel_15));
  Multiplexer #(.width(4), .enable("false")) multiplexer_5 (
    .in0(4'b0000), .in1(4'b0111), .out(multiplexer_5_out), .sel(AluSel_7));
  Multiplexer #(.width(4), .enable("false")) multiplexer_6 (
    .in0(4'b0000), .in1(4'b0110), .out(multiplexer_6_out), .sel(AluSel_6));
  Multiplexer #(.width(4), .enable("false")) multiplexer_7 (
    .in0(4'b0000), .in1(4'b0010), .out(multiplexer_7_out), .sel(AluSel_2));
  Multiplexer #(.width(4), .enable("false")) multiplexer_8 (
    .in0(4'b0000), .in1(4'b1001), .out(multiplexer_8_out), .sel(AluSel_9));
  Multiplexer #(.width(4), .enable("false")) multiplexer_9 (
    .in0(4'b0000), .in1(4'b1000), .out(multiplexer_9_out), .sel(AluSel_8));
  Multiplexer #(.width(4), .enable("false")) multiplexer_10 (
    .in0(4'b0000), .in1(4'b1011), .out(multiplexer_10_out), .sel(AluSel_11));
  Multiplexer #(.width(4), .enable("false")) multiplexer_11 (
    .in0(4'b0000), .in1(4'b0001), .out(multiplexer_11_out), .sel(AluSel_1));
  Multiplexer #(.width(4), .enable("false")) multiplexer_12 (
    .in0(4'b0000), .in1(4'b1010), .out(multiplexer_12_out), .sel(AluSel_10));
  Multiplexer #(.width(4), .enable("false")) multiplexer_13 (
    .in0(4'b0000), .in1(4'b0000), .out(multiplexer_13_out), .sel(AluSel_0));
  assign ALUSel_output = multiplexer_1_out | multiplexer_2_out | multiplexer_3_out | multiplexer_4_out | multiplexer_5_out | multiplexer_6_out | multiplexer_7_out | multiplexer_8_out | multiplexer_9_out | multiplexer_10_out | multiplexer_11_out | multiplexer_12_out | multiplexer_13_out;  // OR_Gate or_1, 4 bits wide

  // Other names for the same wires on the sheet: funct3[2:0] = funct3_input; funct7[6:0] = funct7_input;
  //   Rtype_ALUsel[3:0] = ALUSel_output
endmodule

module Branch_comparator (
  input  [31:0] Input_dataA,
  input  [31:0] Input_dataB,
  input  Input_BrUn,
  output Output_BrEq,
  output Output_BrLT
);

  wire BrLT_signed, BrLT_unsigned;

  Comparator #(.width(32)) comparator_1 (.a(Input_dataA), .b(Input_dataB), .eq(Output_BrEq));  // open: gt, lt
  Comparator #(.width(32)) comparator_2 (.a(Input_dataA), .b(Input_dataB), .lt(BrLT_signed));  // open: gt, eq
  Comparator #(.width(32), .mode("unsigned")) comparator_3 (
    .a(Input_dataA), .b(Input_dataB), .lt(BrLT_unsigned));  // open: gt, eq
  Multiplexer #(.enable("false")) multiplexer_1 (
    .in0(BrLT_signed), .in1(BrLT_unsigned), .out(Output_BrLT), .sel(Input_BrUn));

  // Other names for the same wires on the sheet: BrEq = Output_BrEq; BrLT = Output_BrLT; BrUn = Input_BrUn;
  //   dataA[31:0] = Input_dataA; dataB[31:0] = Input_dataB

  // Notes on the sheet:
  //   Inputs and outputs
  //   Comparator Logic
endmodule
